# Fritzing sketch voltage_divier (saved by Fritzing 0.9.10b)
breadboards: 1

parts:
  R1 = Resistor [tolerance=±5% power=0.25 resistance=220 package=THT]
  R2 = Resistor [tolerance=±5% power=0.25 resistance=220 package=THT]
  부품1 = Arduino Mega 2560 (Rev3)

nets:
  N1: R1.Pin_0, 부품1.5V
  N2: R1.Pin_1, R2.Pin_0, 부품1.A0
  N3: R2.Pin_1, 부품1.GND
