# Fritzing sketch Sonar1 (saved by Fritzing 0.9.10b)
breadboards: 1

parts:
  부품1 = Arduino Mega 2560 (Rev3)
  HC-SR04_Sensor_1 = HC-SR04 Ultrasonic Distance Sensor

nets:
  N1: 부품1.A4, HC-SR04_Sensor_1.VCC
  N2: 부품1.A6, HC-SR04_Sensor_1.GND
  N3: 부품1.D22, HC-SR04_Sensor_1.TRIG
  N4: 부품1.D23, HC-SR04_Sensor_1.ECHO
